# Fritzing sketch ugate (saved by Fritzing 0.6.5b)
breadboards: 1

parts:
  Arduino1 = Arduino
  J1 = Basic Servo
  J2 = Basic Servo
  Q1 = NPN-Transistor [package="TO92 [THT]"]
  R1 = Resistor [tolerance=±5% resistance=1k package=THT]
  Part1 = XBee Explorer Regulated
  Q2 = NPN-Transistor [package="TO92 [THT]"]
  R2 = Resistor [tolerance=±5% resistance=1k package=THT]
  J3 = Basic Servo
  LED1 = RGB LED (com. cathode, rbg) [package="5 mm [THT]"]
  U1 = XBee
  IR_Reciever_(TSOP22)1 = IR Reciever
  J4 = female pin header, 6 pins [form="♀ (female)"]

nets:
  N1: Arduino1.D13, LED1.green_anode
  N2: Arduino1.D12, LED1.blue_anode
  N3: Arduino1.D11, LED1.red_anode
  N4: Arduino1.D2, IR_Reciever_(TSOP22)1.connector2
  N5: Arduino1.D1TX, Part1.DOUT
  N6: Arduino1.D0RX, Part1.DIN
  VCC: Arduino1.+5V, J1.vcc, J2.vcc, J3.vcc
  GND: Arduino1.GND, J1.gnd, J2.gnd, Q1.E, Part1.DIO12, Part1.RTS, Q2.E, J3.gnd, U1.pin5, J4.pin2
  N7: Arduino1.VIN, J4.pin1
  N8: Q1.B, R1.Pin_0
  N9: Part1.GND, Part1.DTR, Part1.RES1
  N10: Part1.RESET, Part1.DIO5, U1.pin6, J4.pin3
  N11: Part1.CTS, Part1.DIO4, Part1.5V, Part1.DIO3
  N12: Q2.B, R2.Pin_0
  N13: U1.pin9, U1.GND
  N14: U1.pin11, U1.pin12

notes:
  12v Battery
  IR Board Plate
  Pin 32
  Cam Pan Servo
  Pin 33
  Cam Tilt Sero
  Microwave Servo
  Pin 31
  TSOP38238 IR Receiver
  Camera
  Pin 39
  Pin 40
  Pin 30
  Microwave Sensor
